# Fritzing sketch splittingTheFlap_Mega2560Shield (saved by Fritzing 0.8.7b)
circuit board: 5cm x 2.5cm
circuit board: 10cm x 15cm
breadboards: 1

parts:
  Part1 = Arduino Mega 2560 (Rev3)
  J244 = Power Jack [package=power_jack_pth]
  U17 = RJ45 Jack [package=rj45-8]  # not connected
  U18 = RJ45 Jack [package=rj45-8]
  U19 = RJ45 Jack [package=rj45-8]
  U20 = RJ45 Jack [package=rj45-8]
  U21 = RJ45 Jack [package=rj45-8]
  U22 = RJ45 Jack [package=rj45-8]
  U23 = RJ45 Jack [package=rj45-8]
  U24 = RJ45 Jack [package=rj45-8]
  U25 = RJ45 Jack [package=rj45-8]
  U26 = RJ45 Jack [package=rj45-8]
  U27 = RJ45 Jack [package=rj45-8]
  U28 = RJ45 Jack [package=rj45-8]
  U29 = RJ45 Jack [package=rj45-8]
  U30 = RJ45 Jack [package=rj45-8]
  U31 = RJ45 Jack [package=rj45-8]
  U32 = RJ45 Jack [package=rj45-8]
  U34 = RJ45 Jack [package=rj45-8]
  R1 = Resistor [tolerance=±5% resistance=220 package=THT]
  R2 = Resistor [tolerance=±5% resistance=220 package=THT]
  U35 = RJ45 Jack [package=rj45-8]  # not connected
  R3 = Resistor [tolerance=±5% resistance=220 package=THT]
  U36 = RJ45 Jack [package=rj45-8]
  J245 = female pin header, 1 pin [form="♀ (female)"]
  J246 = female pin header, 1 pin [form="♀ (female)"]
  J247 = female pin header, 3 pins [form="♀ (female)"]
  J248 = female pin header, 3 pins [form="♀ (female)"]
  J249 = female pin header, 2 pins [form="♀ (female)"]

nets:
  N1: Part1.A8, U30.3
  N2: Part1.A9, U28.3
  N3: Part1.A10, U29.3
  N4: Part1.A11, U20.3
  N5: Part1.A12, U21.3
  N6: Part1.A13, U19.3
  N7: Part1.A0, U27.3
  N8: Part1.A1, U26.3
  N9: Part1.A2, U25.3
  N10: Part1.A3, U23.3
  N11: Part1.A4, U24.3
  N12: Part1.A5, U22.3
  N13: Part1.A6, U18.3
  N14: Part1.A7, U31.3
  N15: Part1.D21/SCL, Part1.SCL, U32.6, U34.6, R1.Pin_1
  N16: Part1.D20/SDA, Part1.SDA, U32.8, U34.8, R2.Pin_1
  N17: Part1.D14/TX3, U23.8
  N18: Part1.D12_PWM, U22.8
  N19: Part1.D11_PWM, U22.6
  N20: Part1.D10_PWM, U22.4
  N21: Part1.D9_PWM, U18.8
  N22: Part1.D8_PWM, U18.6
  N23: Part1.5V, U18.5, U19.5, U20.5, U21.5, U22.5, U23.5, U24.5, U25.5, U26.5, U27.5, U28.5, U29.5, U30.5, U31.5, U32.5, U34.5, R1.Pin_0, R2.Pin_0
  GND: Part1.GND, J244.GND, J244.GNDBREAK, U18.1, U19.1, U20.1, U21.1, U22.1, U23.1, U24.1, U25.1, U26.1, U27.1, U28.1, U29.1, U30.1, U31.1, U32.1, U34.1
  N24: Part1.D2_PWM, U23.6
  N25: Part1.D3_PWM, U23.4
  N26: Part1.D4_PWM, U24.8
  N27: Part1.D5_PWM, U24.6
  N28: Part1.D6_PWM, U24.4
  N29: Part1.D7_PWM, U18.4
  N30: Part1.D22, U28.4
  N31: Part1.D23, U30.8
  N32: Part1.D24, U28.6
  N33: Part1.D25, U30.6
  N34: Part1.D26, U28.8
  N35: Part1.D27, U30.4
  N36: Part1.D28, U29.4
  N37: Part1.D29, U31.8
  N38: Part1.D30, U29.6
  N39: Part1.D31, U31.6
  N40: Part1.D32, U29.8
  N41: Part1.D33, U31.4
  N42: Part1.D34, U27.4
  N43: Part1.D35, U20.8
  N44: Part1.D36, U27.6
  N45: Part1.D37, U20.6
  N46: Part1.D38, U27.8
  N47: Part1.D39, U20.4
  N48: Part1.D40, U26.4
  N49: Part1.D41, U21.8
  N50: Part1.D42, U26.6
  N51: Part1.D43, U21.6
  N52: Part1.D44, U26.8
  N53: Part1.D45, U21.4
  N54: Part1.D46, U25.4
  N55: Part1.D47, U19.8
  N56: Part1.D48, U25.6
  N57: Part1.D49, U19.6
  N58: Part1.D50, U25.8
  N59: Part1.D51, U19.4
  N60: J244.PWR, U18.7, U19.7, U20.7, U21.7, U22.7, U23.7, U24.7, U25.7, U26.7, U27.7, U28.7, U29.7, U30.7, U31.7
  N61: R3.Pin_0, U36.5, J247.pin1
  N62: R3.Pin_1, U36.3, J247.pin3
  N63: U36.1, J247.pin2, J248.pin1, J249.pin1
  N64: U36.2, J246.pin1
  N65: U36.4, J245.pin1
  N66: U36.6, J248.pin2
  N67: U36.7, J249.pin2
  N68: U36.8, J248.pin3

notes:
  24V in
  24V+
  HallAnalog
  5V+
  GND
  Enbl
  Step
  Dir
  I2C
  M1
  M2
  M3
  M4
  M5
  M6
  M7
  M11
  M9
  M8
  M10
  M12
  M14
  M13
  +
  5 V IN
  SDA
  SCL
  hall A0
  step 36
  dir 38
  enbl 34
  hall A1
  hall A2
  hall A3
  hall A4
  hall A5
  hall A6
  hall A7
  hall A8
  hall A9
  hall A10
  hall A11
  hall A12
  hall A13
  dir 12
  step 11
  enbl 10
  enbl 7
  step 8
  dir 9
  enbl 33
  step 31
  dir 29
  enbl 27
  dir 23
  step 25
  dir 26
  step 24
  enbl 22
  dir 32
  enbl 28
  step 30
  enbl 6
  step 5
  dir 4
  step 2
  dir 14
  enbl 3
  20
  21
  1k5
  RJ45
  OH090U
  SLP
  dig
  5+
  +M
  www.marcodemutiis.com
  750
  STEP
  DIR
  ENBL
  enbl 40
  dir 44
  step 42
  enbl 46
  dir 50
  step 48
  enbl 39
  dir 35
  step 37
  enbl 45
  dir 41
  step 43
  enbl 51
  dir 47
  step 49
